// Digital circuit cpu.dig as structural Verilog
module cpu (
  input  [15:0] in_1,
  input  [15:0] in_2,
  input  [15:0] in_5,
  input  [15:0] in_6,
  input  [15:0] in_7,
  input  [15:0] in_8,
  input  [15:0] in_9,
  input  [15:0] in_10,
  input  [1:0] in_11,
  output out_3,
  output [15:0] out_4
);

  wire [15:0] decoder_1_a, undriven;
  wire [31:0] multiplexer_1_out;

  Multiplexer #(.Selector_Bits(2), .Bits(32)) multiplexer_1 (
    .sel(in_11), .in_0({in_2, in_1}), .in_1({in_6, in_5}), .in_2({in_8, in_7}), .in_3({in_10, in_9}),
    .out(multiplexer_1_out));
  Decoder decoder_1 (.Instruction(multiplexer_1_out), .A(decoder_1_a));  // open: rs, rd
  Execute execute_1 (.B(undriven), .A(decoder_1_a), .Result(out_4), .Carry(out_3));
endmodule
